// Logisim project ControlUnit.circ as structural Verilog: 2 circuits, main circuit ControlUnit
module ControlUnit (
  input  [31:0] OP,
  input  CLOCK,
  output WR_PC,
  output WR_RD,
  output RD_DEST,
  output WR_IR,
  output SEL_REG,
  output [1:0] OP_Y_SEL,
  output [3:0] OP_ALU,
  output WR_SR,
  output SEL_D,
  output WR_AR,
  output [1:0] OP_ABI,
  output [2:0] OP_DBI,
  output EN_D,
  output EN_A,
  output RD,
  output WR
);

  wire multiplexer_2_out;
  wire [15:0] multiplexer_1_out, optoaddr_1_nextop_addr, register_1_q, rom_1_data;
  wire [63:23] rom_1_data_2;

  Register #(.width(16)) register_1 (.D(rom_1_data), .en(1'b1), .clk(CLOCK), .Q(register_1_q));  // open: clr
  OpToAddr optoaddr_1 (.OP(OP), .NextOp_Addr(optoaddr_1_nextop_addr));
  Multiplexer #(.width(16)) multiplexer_1 (
    .in0(register_1_q), .in1(optoaddr_1_nextop_addr), .out(multiplexer_1_out), .sel(multiplexer_2_out));
  Multiplexer multiplexer_2 (.in0(1'b0), .in1(rom_1_data_2[23]), .out(multiplexer_2_out), .sel(1'b1));
  ROM #(.addrWidth(16), .dataWidth(64)) rom_1 (
    .addr(multiplexer_1_out),
    .data({rom_1_data_2[63:40], rom_1_data, rom_1_data_2[23], WR, RD, EN_A, EN_D, OP_DBI, OP_ABI, WR_AR, SEL_D, WR_SR, OP_ALU, OP_Y_SEL, SEL_REG, WR_IR, RD_DEST, WR_RD, WR_PC}));

  // Notes on the sheet:
  //   Init
endmodule

module OpToAddr (
  input  [31:0] OP,
  output [15:0] NextOp_Addr
);

  ROM #(.dataWidth(16)) rom_1 (.addr(OP[31:24]), .data(NextOp_Addr));
endmodule
