// Logisim project M32.circ as structural Verilog
module PC (
  input  [31:0] INPT,
  input  WR,
  output [31:0] OUTPT
);

  wire check_on_machine_1_addr_cero, CLK_out, wait3_1_out_2;
  wire [31:0] register_1_q;

  Clock CLK (.out(CLK_out));
  Wait3 wait3_1 (.CLK(CLK_out), .out_2(wait3_1_out_2));
  Register #(.width(32)) register_1 (.D(INPT), .en(WR), .clk(CLK_out), .Q(register_1_q));  // open: clr
  Multiplexer #(.width(32)) multiplexer_1 (
    .in0({32{1'b0}}), .in1(register_1_q), .out(OUTPT), .sel(check_on_machine_1_addr_cero));
  Check_On_Machine check_on_machine_1 (
    .CLK(CLK_out), .WR(WR), .NRESET(wait3_1_out_2), .ADDR_CERO(check_on_machine_1_addr_cero));
endmodule

module RBANK (
  input  [31:0] Rd,
  input  CLK,
  input  [4:0] s1,
  input  [4:0] s2,
  input  WR,
  input  [4:0] d,
  output [31:0] Rs1,
  output [31:0] Rs2
);

  wire decoder_1_out1, decoder_1_out2, decoder_1_out3, decoder_1_out4, decoder_1_out5, decoder_1_out6,
       decoder_1_out7, decoder_1_out8, decoder_1_out9, decoder_1_out10, decoder_1_out11, decoder_1_out12,
       decoder_1_out13, decoder_1_out14, decoder_1_out15, decoder_1_out16, decoder_1_out17, decoder_1_out18,
       decoder_1_out19, decoder_1_out20, decoder_1_out21, decoder_1_out22, decoder_1_out23, decoder_1_out24,
       decoder_1_out25, decoder_1_out26, decoder_1_out27, decoder_1_out28, decoder_1_out29, decoder_1_out30,
       decoder_1_out31;
  wire [31:0] register_1_q, register_2_q, register_3_q, register_4_q, register_5_q, register_6_q,
       register_7_q, register_8_q, register_9_q, register_10_q, register_11_q, register_12_q, register_13_q,
       register_14_q, register_15_q, register_16_q, register_17_q, register_18_q, register_19_q,
       register_20_q, register_21_q, register_22_q, register_23_q, register_24_q, register_25_q,
       register_26_q, register_27_q, register_28_q, register_29_q, register_30_q, register_31_q;

  Decoder #(.select(5)) decoder_1 (
    .out1(decoder_1_out1), .out2(decoder_1_out2), .out3(decoder_1_out3), .out4(decoder_1_out4),
    .out5(decoder_1_out5), .out6(decoder_1_out6), .out7(decoder_1_out7), .out8(decoder_1_out8),
    .out9(decoder_1_out9), .out10(decoder_1_out10), .out11(decoder_1_out11), .out12(decoder_1_out12),
    .out13(decoder_1_out13), .out14(decoder_1_out14), .out15(decoder_1_out15), .out16(decoder_1_out16),
    .out17(decoder_1_out17), .out18(decoder_1_out18), .out19(decoder_1_out19), .out20(decoder_1_out20),
    .out21(decoder_1_out21), .out22(decoder_1_out22), .out23(decoder_1_out23), .out24(decoder_1_out24),
    .out25(decoder_1_out25), .out26(decoder_1_out26), .out27(decoder_1_out27), .out28(decoder_1_out28),
    .out29(decoder_1_out29), .out30(decoder_1_out30), .out31(decoder_1_out31), .sel(d), .en(WR));  // open: out0
  Register #(.width(32)) register_1 (.D(Rd), .en(decoder_1_out1), .clk(CLK), .Q(register_1_q));  // open: clr
  Register #(.width(32)) register_2 (.D(Rd), .en(decoder_1_out2), .clk(CLK), .Q(register_2_q));  // open: clr
  Register #(.width(32)) register_3 (.D(Rd), .en(decoder_1_out3), .clk(CLK), .Q(register_3_q));  // open: clr
  Register #(.width(32)) register_4 (.D(Rd), .en(decoder_1_out4), .clk(CLK), .Q(register_4_q));  // open: clr
  Register #(.width(32)) register_5 (.D(Rd), .en(decoder_1_out5), .clk(CLK), .Q(register_5_q));  // open: clr
  Register #(.width(32)) register_6 (.D(Rd), .en(decoder_1_out6), .clk(CLK), .Q(register_6_q));  // open: clr
  Register #(.width(32)) register_7 (.D(Rd), .en(decoder_1_out7), .clk(CLK), .Q(register_7_q));  // open: clr
  Register #(.width(32)) register_8 (.D(Rd), .en(decoder_1_out8), .clk(CLK), .Q(register_8_q));  // open: clr
  Register #(.width(32)) register_9 (.D(Rd), .en(decoder_1_out9), .clk(CLK), .Q(register_9_q));  // open: clr
  Register #(.width(32)) register_10 (.D(Rd), .en(decoder_1_out10), .clk(CLK), .Q(register_10_q));  // open: clr
  Register #(.width(32)) register_11 (.D(Rd), .en(decoder_1_out11), .clk(CLK), .Q(register_11_q));  // open: clr
  Register #(.width(32)) register_12 (.D(Rd), .en(decoder_1_out12), .clk(CLK), .Q(register_12_q));  // open: clr
  Register #(.width(32)) register_13 (.D(Rd), .en(decoder_1_out13), .clk(CLK), .Q(register_13_q));  // open: clr
  Register #(.width(32)) register_14 (.D(Rd), .en(decoder_1_out14), .clk(CLK), .Q(register_14_q));  // open: clr
  Register #(.width(32)) register_15 (.D(Rd), .en(decoder_1_out15), .clk(CLK), .Q(register_15_q));  // open: clr
  Register #(.width(32)) register_16 (.D(Rd), .en(decoder_1_out16), .clk(CLK), .Q(register_16_q));  // open: clr
  Register #(.width(32)) register_17 (.D(Rd), .en(decoder_1_out17), .clk(CLK), .Q(register_17_q));  // open: clr
  Register #(.width(32)) register_18 (.D(Rd), .en(decoder_1_out18), .clk(CLK), .Q(register_18_q));  // open: clr
  Register #(.width(32)) register_19 (.D(Rd), .en(decoder_1_out19), .clk(CLK), .Q(register_19_q));  // open: clr
  Register #(.width(32)) register_20 (.D(Rd), .en(decoder_1_out20), .clk(CLK), .Q(register_20_q));  // open: clr
  Register #(.width(32)) register_21 (.D(Rd), .en(decoder_1_out21), .clk(CLK), .Q(register_21_q));  // open: clr
  Register #(.width(32)) register_22 (.D(Rd), .en(decoder_1_out22), .clk(CLK), .Q(register_22_q));  // open: clr
  Register #(.width(32)) register_23 (.D(Rd), .en(decoder_1_out23), .clk(CLK), .Q(register_23_q));  // open: clr
  Register #(.width(32)) register_24 (.D(Rd), .en(decoder_1_out24), .clk(CLK), .Q(register_24_q));  // open: clr
  Register #(.width(32)) register_25 (.D(Rd), .en(decoder_1_out25), .clk(CLK), .Q(register_25_q));  // open: clr
  Register #(.width(32)) register_26 (.D(Rd), .en(decoder_1_out26), .clk(CLK), .Q(register_26_q));  // open: clr
  Register #(.width(32)) register_27 (.D(Rd), .en(decoder_1_out27), .clk(CLK), .Q(register_27_q));  // open: clr
  Register #(.width(32)) register_28 (.D(Rd), .en(decoder_1_out28), .clk(CLK), .Q(register_28_q));  // open: clr
  Register #(.width(32)) register_29 (.D(Rd), .en(decoder_1_out29), .clk(CLK), .Q(register_29_q));  // open: clr
  Register #(.width(32)) register_30 (.D(Rd), .en(decoder_1_out30), .clk(CLK), .Q(register_30_q));  // open: clr
  Register #(.width(32)) register_31 (.D(Rd), .en(decoder_1_out31), .clk(CLK), .Q(register_31_q));  // open: clr
  Multiplexer #(.select(5), .width(32)) multiplexer_1 (
    .in0({32{1'b0}}), .in1(register_1_q), .in2(register_2_q), .in3(register_3_q), .in4(register_4_q),
    .in5(register_5_q), .in6(register_6_q), .in7(register_7_q), .in8(register_8_q), .in9(register_9_q),
    .in10(register_10_q), .in11(register_11_q), .in12(register_12_q), .in13(register_13_q),
    .in14(register_14_q), .in15(register_15_q), .in16(register_16_q), .in17(register_17_q),
    .in18(register_18_q), .in19(register_19_q), .in20(register_20_q), .in21(register_21_q),
    .in22(register_22_q), .in23(register_23_q), .in24(register_24_q), .in25(register_25_q),
    .in26(register_26_q), .in27(register_27_q), .in28(register_28_q), .in29(register_29_q),
    .in30(register_30_q), .in31(register_31_q), .out(Rs2), .sel(s2));
  Multiplexer #(.select(5), .width(32)) multiplexer_2 (
    .in0({32{1'b0}}), .in1(register_1_q), .in2(register_2_q), .in3(register_3_q), .in4(register_4_q),
    .in5(register_5_q), .in6(register_6_q), .in7(register_7_q), .in8(register_8_q), .in9(register_9_q),
    .in10(register_10_q), .in11(register_11_q), .in12(register_12_q), .in13(register_13_q),
    .in14(register_14_q), .in15(register_15_q), .in16(register_16_q), .in17(register_17_q),
    .in18(register_18_q), .in19(register_19_q), .in20(register_20_q), .in21(register_21_q),
    .in22(register_22_q), .in23(register_23_q), .in24(register_24_q), .in25(register_25_q),
    .in26(register_26_q), .in27(register_27_q), .in28(register_28_q), .in29(register_29_q),
    .in30(register_30_q), .in31(register_31_q), .out(Rs1), .sel(s1));
endmodule

module BRANCHUNIT (
  input  [31:0] OP,
  input  [3:0] in_2,
  output BR
);

  wire and_1_out, and_2_out, and_3_out, and_4_out, and_5_out, and_6_out, and_7_out, and_8_out, and_9_out,
       and_10_out, and_11_out, and_12_out, and_13_out, and_14_out, and_15_out, and_16_out, and_17_out,
       not_1_out, not_2_out, not_3_out, not_4_out, or_1_out, or_2_out, or_3_out, or_4_out, or_5_out,
       or_6_out, or_7_out, selecsalto_1_q0, selecsalto_1_q1, selecsalto_1_q2, selecsalto_1_q3,
       selecsalto_1_q4, selecsalto_1_q5, selecsalto_1_q6, selecsalto_1_q7, selecsalto_1_q8, selecsalto_1_q9;

  SELECSALTO selecsalto_1 (
    .INPT(OP), .q0(selecsalto_1_q0), .q1(selecsalto_1_q1), .q2(selecsalto_1_q2), .q3(selecsalto_1_q3),
    .q4(selecsalto_1_q4), .q5(selecsalto_1_q5), .q6(selecsalto_1_q6), .q7(selecsalto_1_q7),
    .q8(selecsalto_1_q8), .q9(selecsalto_1_q9));
  not not_1 (not_1_out, in_2[0]);
  not not_2 (not_2_out, in_2[1]);
  not not_3 (not_3_out, in_2[2]);
  not not_4 (not_4_out, in_2[3]);
  and and_1 (and_1_out, in_2[3], selecsalto_1_q0);
  and and_2 (and_2_out, not_4_out, selecsalto_1_q1);
  and and_3 (and_3_out, not_3_out, not_2_out);
  and and_4 (and_4_out, in_2[2], in_2[1]);
  and and_5 (and_5_out, not_2_out, not_3_out);
  and and_6 (and_6_out, in_2[1], in_2[2]);
  and and_7 (and_7_out, not_2_out, in_2[2]);
  and and_8 (and_8_out, in_2[1], not_4_out, selecsalto_1_q4);
  and and_9 (and_9_out, not_2_out, in_2[2]);
  and and_10 (and_10_out, in_2[1], not_3_out);
  and and_11 (and_11_out, in_2[0], not_4_out, selecsalto_1_q6);
  and and_12 (and_12_out, in_2[0], selecsalto_1_q7);
  and and_13 (and_13_out, not_1_out, selecsalto_1_q8);
  or or_1 (or_1_out, not_1_out, in_2[3]);
  or or_2 (or_2_out, and_3_out, and_4_out);
  or or_3 (or_3_out, and_5_out, and_6_out);
  or or_4 (or_4_out, and_7_out, and_8_out);
  or or_5 (or_5_out, and_9_out, in_2[3], and_10_out);
  and and_14 (and_14_out, or_1_out, selecsalto_1_q9);
  and and_15 (and_15_out, or_2_out, not_4_out, selecsalto_1_q2);
  and and_16 (and_16_out, or_3_out, selecsalto_1_q3);
  and and_17 (and_17_out, or_5_out, selecsalto_1_q5);
  or or_6 (or_6_out, and_1_out, and_2_out, and_15_out, and_16_out);
  or or_7 (or_7_out, and_11_out, and_12_out, and_13_out, and_14_out);
  or or_8 (BR, or_6_out, or_4_out, and_17_out, or_7_out);
endmodule

module ABI (
  input  [31:0] AIN,
  input  [1:0] OP,
  output [29:0] out_3,
  output [3:0] out_4
);

  wire and_1_out, and_2_out, and_3_out, and_4_out, and_5_out, and_6_out, and_7_out, and_8_out, and_9_out,
       and_10_out, not_1_out, not_2_out, not_3_out, not_4_out;

  not not_1 (not_1_out, OP[1]);
  not not_2 (not_2_out, OP[0]);
  not not_3 (not_3_out, AIN[1]);
  not not_4 (not_4_out, AIN[0]);
  and and_1 (and_1_out, not_1_out, not_2_out, not_3_out, not_4_out);
  and and_2 (and_2_out, not_1_out, OP[0], AIN[1], not_4_out);
  and and_3 (and_3_out, OP[1], not_2_out, AIN[1], AIN[0]);
  and and_4 (and_4_out, not_1_out, not_2_out, not_3_out, not_4_out);
  and and_5 (and_5_out, not_1_out, OP[0], AIN[1], not_4_out);
  and and_6 (and_6_out, OP[1], not_2_out, AIN[1], not_4_out);
  and and_7 (and_7_out, not_1_out, not_3_out, not_4_out);
  and and_8 (and_8_out, OP[1], not_2_out, not_3_out, AIN[0]);
  and and_9 (and_9_out, not_2_out, not_3_out, not_4_out);
  and and_10 (and_10_out, not_1_out, not_3_out, not_4_out);
  or or_1 (out_4[0], and_1_out, and_2_out, and_3_out);
  or or_2 (out_4[1], and_4_out, and_5_out, and_6_out);
  or or_3 (out_4[2], and_7_out, and_8_out);
  or or_4 (out_4[3], and_9_out, and_10_out);

  assign out_3 = AIN[31:2];
endmodule

module ALU (
  input  [31:0] YPrima,
  input  [31:0] XPrima,
  input  Carry,
  input  [3:0] OP,
  output [31:0] Z
);

  wire subcarry_1_carryprima;
  wire [3:0] and32_1_out_2;
  wire [31:0] adder_1_out, and_1_out, or_1_out, sll_alu_1_z, sra_alu_1_z, srl_alu_1_z, subcarry_1_outpt,
       xor_1_out;

  SUBCARRY subcarry_1 (
    .YPrima(YPrima), .OP(OP), .Carry(Carry), .OUTPT(subcarry_1_outpt), .CarryPrima(subcarry_1_carryprima));
  assign xor_1_out = XPrima ^ subcarry_1_outpt;  // XOR_Gate xor_1, 32 bits wide
  assign or_1_out = XPrima | subcarry_1_outpt;  // OR_Gate or_1, 32 bits wide
  assign and_1_out = XPrima & subcarry_1_outpt;  // AND_Gate and_1, 32 bits wide
  Adder #(.width(32)) adder_1 (
    .a(XPrima), .b(subcarry_1_outpt), .out(adder_1_out), .cin(subcarry_1_carryprima), .cout(and32_1_out_2[3]));
  SRA_ALU sra_alu_1 (.X(XPrima), .Y(subcarry_1_outpt), .Z(sra_alu_1_z));
  SRL_ALU srl_alu_1 (.X(XPrima), .Y(subcarry_1_outpt), .Z(srl_alu_1_z));
  SLL_ALU sll_alu_1 (.X(XPrima), .Y(subcarry_1_outpt), .Z(sll_alu_1_z));
  Multiplexer #(.select(4), .width(32)) multiplexer_1 (
    .in0(adder_1_out), .in1(adder_1_out), .in2(adder_1_out), .in3(adder_1_out), .in4(and_1_out),
    .in5(or_1_out), .in6(xor_1_out), .in7(sll_alu_1_z), .in8(srl_alu_1_z), .in9(sra_alu_1_z), .out(Z),
    .sel(OP));  // open: in10, in11, in12, in13, in14, in15
  AND32 and32_1 (.X(Z), .out_2(and32_1_out_2[0]));
endmodule

module IR (
  input  [31:0] INPT,
  input  CLOCK,
  input  WRIR,
  output [31:0] OUTPT
);

  Register #(.width(32)) register_1 (.D(INPT), .en(WRIR), .clk(CLOCK), .Q(OUTPT));  // open: clr
endmodule

module RSEL (
  input  [31:0] I,
  input  RDDEST,
  output [4:0] d,
  output [4:0] s1,
  output [4:0] s2
);

  Multiplexer #(.width(5)) multiplexer_1 (.in0(I[23:19]), .in1(I[18:14]), .out(s1), .sel(RDDEST));

  assign d = I[23:19];
  assign s2 = I[12:8];
endmodule

module YSEL (
  input  [31:0] REGS,
  input  [31:0] INST,
  input  [1:0] OPYSEL,
  output [31:0] out_4
);

  wire [31:0] multiplexer_1_out;

  Multiplexer #(.width(32)) multiplexer_1 (
    .in0(REGS), .in1({{20{INST[12]}}, INST[11:0]}), .out(multiplexer_1_out), .sel(INST[14]));
  Multiplexer #(.select(2), .width(32)) multiplexer_2 (
    .in0({32{1'b0}}), .in1(32'h4), .in2(multiplexer_1_out), .in3({{9{INST[23]}}, INST[22:0]}), .out(out_4),
    .sel(OPYSEL));
endmodule

module SR (
  input  [3:0] INPT,
  input  WR_SR,
  input  CLK,
  output [3:0] OUTPT
);

  Register #(.width(4)) register_1 (.D(INPT), .en(WR_SR), .clk(CLK), .Q(OUTPT));  // open: clr
endmodule

module SELECSALTO (
  input  [31:0] INPT,
  output q0,
  output q1,
  output q2,
  output q3,
  output q4,
  output q5,
  output q6,
  output q7,
  output q8,
  output q9
);

  wire and_1_out, and_2_out, and_3_out, and_4_out, and_5_out, and_6_out, and_7_out, and_8_out, and_9_out,
       and_10_out, chipselec_1_outp, not_1_out, not_2_out, not_3_out, not_4_out;

  CHIPSELEC chipselec_1 (.A(INPT), .OUTP(chipselec_1_outp));
  not not_1 (not_1_out, INPT[3]);
  not not_2 (not_2_out, INPT[2]);
  not not_3 (not_3_out, INPT[1]);
  not not_4 (not_4_out, INPT[0]);
  and and_1 (and_1_out, INPT[0], not_3_out, INPT[2], not_1_out);
  and and_2 (and_2_out, not_4_out, INPT[1], INPT[2], not_1_out);
  and and_3 (and_3_out, INPT[0], INPT[1], INPT[2], not_1_out);
  and and_4 (and_4_out, not_4_out, not_3_out, not_2_out, INPT[3]);
  and and_5 (and_5_out, INPT[0], not_3_out, not_2_out, INPT[3]);
  and and_6 (and_6_out, not_4_out, INPT[1], not_2_out, INPT[3]);
  and and_7 (and_7_out, INPT[0], INPT[1], not_2_out, INPT[3]);
  and and_8 (and_8_out, not_4_out, not_3_out, INPT[2], INPT[3]);
  and and_9 (and_9_out, INPT[0], not_3_out, INPT[2], INPT[3]);
  and and_10 (and_10_out, not_4_out, INPT[1], INPT[2], INPT[3]);
  and and_11 (q0, and_1_out, chipselec_1_outp, INPT[4]);
  and and_12 (q1, chipselec_1_outp, and_2_out, INPT[4]);
  and and_13 (q2, and_3_out, chipselec_1_outp, INPT[4]);
  and and_14 (q3, and_4_out, chipselec_1_outp, INPT[4]);
  and and_15 (q4, and_5_out, chipselec_1_outp, INPT[4]);
  and and_16 (q5, and_6_out, chipselec_1_outp, INPT[4]);
  and and_17 (q6, and_7_out, chipselec_1_outp, INPT[4]);
  and and_18 (q7, and_8_out, chipselec_1_outp, INPT[4]);
  and and_19 (q8, and_9_out, chipselec_1_outp, INPT[4]);
  and and_20 (q9, and_10_out, chipselec_1_outp, INPT[4]);
endmodule

module CHIPSELEC (
  input  [31:0] A,
  output OUTP
);

  nor nor_1 (OUTP, A[5], A[6], A[7], A[8], A[9], A[10], A[11], A[12], A[13], A[14], A[15], A[16], A[17], A[18], A[19], A[20], A[21], A[22], A[23], A[24], A[25], A[26], A[27], A[28], A[29], A[30], A[31]);
endmodule

module SUBCARRY (
  input  [31:0] YPrima,
  input  [3:0] OP,
  input  Carry,
  output [31:0] OUTPT,
  output CarryPrima
);

  wire check_1_carry, check_1_sub;
  wire [31:0] adder_1_out, not_1_out;

  assign not_1_out = ~YPrima;  // NOT_Gate not_1, 32 bits wide
  Adder #(.width(32)) adder_1 (.a(not_1_out), .b(32'h1), .out(adder_1_out));  // open: cin, cout
  CHECK check_1 (.INPT(OP), .SUB(check_1_sub), .CARRY(check_1_carry));
  Multiplexer #(.width(32)) multiplexer_1 (.in0(YPrima), .in1(adder_1_out), .out(OUTPT), .sel(check_1_sub));
  and and_1 (CarryPrima, check_1_carry, Carry);
endmodule

module CHECK (
  input  [3:0] INPT,
  output SUB,
  output CARRY
);

  wire not_1_out, not_2_out;

  not not_1 (not_1_out, INPT[3]);
  not not_2 (not_2_out, INPT[2]);
  and and_1 (SUB, INPT[1], not_2_out, not_1_out);
  and and_2 (CARRY, INPT[0], not_2_out, not_1_out);
endmodule

module SRA_ALU (
  input  [31:0] X,
  input  [31:0] Y,
  output [31:0] Z
);

  wire [31:0] sra2_1_y, sra4_1_y, sra8_1_y, sra16_1_y;

  SRA16 sra16_1 (.X(X), .Enable(Y[4]), .Y(sra16_1_y));
  SRA8 sra8_1 (.X(sra16_1_y), .Enable(Y[3]), .Y(sra8_1_y));
  SRA4 sra4_1 (.X(sra8_1_y), .Enable(Y[2]), .Y(sra4_1_y));
  SRA2 sra2_1 (.X(sra4_1_y), .Enable(Y[1]), .Y(sra2_1_y));
  SRA1 sra1_1 (.X(sra2_1_y), .Enable(Y[0]), .Y(Z));
endmodule

module SRL_ALU (
  input  [31:0] X,
  input  [31:0] Y,
  output [31:0] Z
);

  wire [31:0] srl2_1_y, srl4_1_y, srl8_1_y, srl16_1_y;

  SRL16 srl16_1 (.X(X), .Enable(Y[4]), .Y(srl16_1_y));
  SRL8 srl8_1 (.X(srl16_1_y), .Enable(Y[3]), .Y(srl8_1_y));
  SRL4 srl4_1 (.X(srl8_1_y), .Enable(Y[2]), .Y(srl4_1_y));
  SRL2 srl2_1 (.X(srl4_1_y), .Enable(Y[1]), .Y(srl2_1_y));
  SRL1 srl1_1 (.X(srl2_1_y), .Enable(Y[0]), .Y(Z));
endmodule

module SLL_ALU (
  input  [31:0] X,
  input  [31:0] Y,
  output [31:0] Z
);

  wire [31:0] sll2_1_y, sll4_1_y, sll8_1_y, sll16_1_y;

  SLL16 sll16_1 (.X(X), .Enable(Y[4]), .Y(sll16_1_y));
  SLL8 sll8_1 (.X(sll16_1_y), .Enable(Y[3]), .Y(sll8_1_y));
  SLL4 sll4_1 (.X(sll8_1_y), .Enable(Y[2]), .Y(sll4_1_y));
  SLL2 sll2_1 (.X(sll4_1_y), .Enable(Y[1]), .Y(sll2_1_y));
  SLL1 sll1_1 (.X(sll2_1_y), .Enable(Y[0]), .Y(Z));
endmodule

module SRA16 (
  input  [31:0] X,
  input  Enable,
  output [31:0] Y
);

  SRAX srax_1 (.X(X), .COUNT(5'b10000), .Enable(Enable), .OUTPT(Y));
endmodule

module SRA8 (
  input  [31:0] X,
  input  Enable,
  output [31:0] Y
);

  SRAX srax_1 (.X(X), .COUNT(5'b01000), .Enable(Enable), .OUTPT(Y));
endmodule

module SRA4 (
  input  [31:0] X,
  input  Enable,
  output [31:0] Y
);

  SRAX srax_1 (.X(X), .COUNT(5'b00100), .Enable(Enable), .OUTPT(Y));
endmodule

module SRA2 (
  input  [31:0] X,
  input  Enable,
  output [31:0] Y
);

  SRAX srax_1 (.X(X), .COUNT(5'b00010), .Enable(Enable), .OUTPT(Y));
endmodule

module SRA1 (
  input  [31:0] X,
  input  Enable,
  output [31:0] Y
);

  SRAX srax_1 (.X(X), .COUNT(5'b00001), .Enable(Enable), .OUTPT(Y));
endmodule

module SRL16 (
  input  [31:0] X,
  input  Enable,
  output [31:0] Y
);

  SRLX srlx_1 (.X(X), .COUNT(5'b10000), .Enable(Enable), .OUTPT(Y));
endmodule

module SRL8 (
  input  [31:0] X,
  input  Enable,
  output [31:0] Y
);

  SRLX srlx_1 (.X(X), .COUNT(5'b01000), .Enable(Enable), .OUTPT(Y));
endmodule

module SRL4 (
  input  [31:0] X,
  input  Enable,
  output [31:0] Y
);

  SRLX srlx_1 (.X(X), .COUNT(5'b00100), .Enable(Enable), .OUTPT(Y));
endmodule

module SRL2 (
  input  [31:0] X,
  input  Enable,
  output [31:0] Y
);

  SRLX srlx_1 (.X(X), .COUNT(5'b00010), .Enable(Enable), .OUTPT(Y));
endmodule

module SRL1 (
  input  [31:0] X,
  input  Enable,
  output [31:0] Y
);

  SRLX srlx_1 (.X(X), .COUNT(5'b00001), .Enable(Enable), .OUTPT(Y));
endmodule

module SLL16 (
  input  [31:0] X,
  input  Enable,
  output [31:0] Y
);

  SLLX sllx_1 (.X(X), .COUNT(5'b10000), .Enable(Enable), .OUTPT(Y));
endmodule

module SLL8 (
  input  [31:0] X,
  input  Enable,
  output [31:0] Y
);

  SLLX sllx_1 (.X(X), .COUNT(5'b01000), .Enable(Enable), .OUTPT(Y));
endmodule

module SLL4 (
  input  [31:0] X,
  input  Enable,
  output [31:0] Y
);

  SLLX sllx_1 (.X(X), .COUNT(5'b00100), .Enable(Enable), .OUTPT(Y));
endmodule

module SLL2 (
  input  [31:0] X,
  input  Enable,
  output [31:0] Y
);

  SLLX sllx_1 (.X(X), .COUNT(5'b00010), .Enable(Enable), .OUTPT(Y));
endmodule

module SLL1 (
  input  [31:0] X,
  input  Enable,
  output [31:0] Y
);

  SLLX sllx_1 (.X(X), .COUNT(5'b00001), .Enable(Enable), .OUTPT(Y));
endmodule

module SRAX (
  input  [31:0] X,
  input  [4:0] COUNT,
  input  Enable,
  output [31:0] OUTPT
);

  wire [31:0] shifter_1_out;

  Shifter #(.shift("ar"), .width(32)) shifter_1 (.in(X), .\dist (COUNT), .out(shifter_1_out));
  Multiplexer #(.width(32)) multiplexer_1 (.in0(X), .in1(shifter_1_out), .out(OUTPT), .sel(Enable));
endmodule

module SRLX (
  input  [31:0] X,
  input  [4:0] COUNT,
  input  Enable,
  output [31:0] OUTPT
);

  wire [31:0] shifter_1_out;

  Shifter #(.shift("lr"), .width(32)) shifter_1 (.in(X), .\dist (COUNT), .out(shifter_1_out));
  Multiplexer #(.width(32)) multiplexer_1 (.in0(X), .in1(shifter_1_out), .out(OUTPT), .sel(Enable));
endmodule

module SLLX (
  input  [31:0] X,
  input  [4:0] COUNT,
  input  Enable,
  output [31:0] OUTPT
);

  wire [31:0] shifter_1_out;

  Shifter #(.width(32)) shifter_1 (.in(X), .\dist (COUNT), .out(shifter_1_out));
  Multiplexer #(.width(32)) multiplexer_1 (.in0(X), .in1(shifter_1_out), .out(OUTPT), .sel(Enable));
endmodule

module AND32 (
  input  [31:0] X,
  output out_2
);

  and and_1 (out_2, X[0], X[1], X[2], X[3], X[4], X[5], X[6], X[7], X[8], X[9], X[10], X[11], X[12], X[13], X[14], X[15], X[16], X[17], X[18], X[19], X[20], X[21], X[22], X[23], X[24], X[25], X[26], X[27], X[28], X[29], X[30], X[31]);
endmodule

module AR (
  input  [31:0] INPT,
  input  WR_AR,
  input  CLK,
  output [31:0] OUTPT
);

  Register #(.width(32)) register_1 (.D(INPT), .en(WR_AR), .clk(CLK), .Q(OUTPT));  // open: clr
endmodule

module Check_On_Machine (
  input  CLK,
  input  WR,
  input  NRESET,
  output ADDR_CERO
);

  wire d_ff_1_q, or_1_out;

  D_Flip_Flop d_ff_1 (.D(or_1_out), .clk(CLK), .Q(d_ff_1_q));  // open: Qn, preset, reset
  or or_1 (or_1_out, d_ff_1_q, WR);
  Multiplexer multiplexer_1 (.in0(1'b0), .in1(or_1_out), .out(ADDR_CERO), .sel(NRESET));
endmodule

module Wait3 (
  input  CLK,
  output out_2
);

  wire comparator_1_eq, comparator_1_gt, not_1_out;
  wire [7:0] adder_1_out, register_1_q;

  Register register_1 (.D(adder_1_out), .en(not_1_out), .clk(CLK), .Q(register_1_q));  // open: clr
  Adder adder_1 (.a(register_1_q), .b(8'h1), .out(adder_1_out));  // open: cin, cout
  Comparator comparator_1 (.a(register_1_q), .b(8'h3), .gt(comparator_1_gt), .eq(comparator_1_eq));  // open: lt
  or or_1 (out_2, comparator_1_gt, comparator_1_eq);
  not not_1 (not_1_out, out_2);
endmodule
